// Logisim project processor.circ as structural Verilog: 4 circuits, main circuit main
module main (
);

  wire aluflag, clk, clr, enIR, enPC, enRewrite, memEnable, memLoadStore, Memory_Clear_out, not_1_out,
       selectMUXA, selectMUXB, selectMUXPC, selectMUXY, Store;
  wire [2:0] selectRA, selectRB, selectRC;
  wire [3:0] ALU_select;
  wire [4:0] Opcode;
  wire [15:0] adder_1_out, bit_extender_1_out, bit_extender_2_out, multiplexer_3_out, multiplexer_4_out, PC;
  wire [27:9] control_unit_1_output_signals;
  wire [31:0] alu_1_output_alu, Immediate, Instruction_Register_q, IRin, multiplexer_1_out,
       multiplexer_2_out, RA_q, RB_q, rf_1_output_ra, rf_1_output_rb, RMout, RY_q, RZ;

  Register #(.width(32)) RA (.D(rf_1_output_ra), .en(1'b1), .Q(RA_q), .clk(clk), .clr(clr));
  RF rf_1 (
    .clock(clk), .clear(clr), .Enable_Writeback(enRewrite), .selectRA(selectRA), .selectRB(selectRB),
    .selectRC(selectRC), .Input_RC(RY_q), .Output_RA(rf_1_output_ra), .Output_RB(rf_1_output_rb),
    .Store(Store));
  Register #(.width(32)) RB (.D(rf_1_output_rb), .en(1'b1), .Q(RB_q), .clk(clk), .clr(clr));
  Multiplexer #(.width(32), .enable("false")) multiplexer_1 (
    .in0(RB_q), .in1(Immediate), .out(multiplexer_1_out), .sel(selectMUXB));
  ALU alu_1 (
    .Input_A(RA_q), .Input_B(multiplexer_1_out), .Output_ALU(alu_1_output_alu),
    .ALU_Control_Signal(ALU_select), .out_5(aluflag));
  Register #(.width(32)) u_RZ (.D(alu_1_output_alu), .en(1'b1), .Q(RZ), .clk(clk), .clr(clr));
  Multiplexer #(.width(32), .enable("false")) multiplexer_2 (
    .in0(RZ), .in1(IRin), .out(multiplexer_2_out), .sel(selectMUXY));
  Register #(.width(32)) RY (.D(multiplexer_2_out), .en(1'b1), .Q(RY_q), .clk(clk), .clr(clr));
  Clock sysclk (.out(clk));
  Register #(.width(32)) RM (.D(RB_q), .en(1'b1), .Q(RMout), .clk(clk), .clr(clr));
  Register #(.width(32)) Instruction_Register (.D(IRin), .en(enIR), .Q(Instruction_Register_q), .clk(clk), .clr(clr));
  Bit_Extender #(.in_width(32)) bit_extender_1 (.in(RZ), .out(bit_extender_1_out));
  Multiplexer #(.width(16), .enable("false")) multiplexer_3 (
    .in0(bit_extender_1_out), .in1(adder_1_out), .out(multiplexer_3_out), .sel(selectMUXPC));
  Register #(.width(16)) u_PC (.D(multiplexer_3_out), .en(enPC), .Q(PC), .clk(clk), .clr(clr));
  Adder #(.width(16)) adder_1 (.a(PC), .b(16'h1), .out(adder_1_out));  // open: cin, cout
  Control_Unit control_unit_1 (
    .IR(Instruction_Register_q), .Clear(clr), .Immediate(Immediate),
    .Output_Signals({ALU_select, control_unit_1_output_signals[27:25], Store, control_unit_1_output_signals[23:21], selectRC, control_unit_1_output_signals[17], selectRB, control_unit_1_output_signals[13], selectRA, control_unit_1_output_signals[9], enPC, enRewrite, enIR, selectMUXPC, selectMUXY, selectMUXB, selectMUXA, memLoadStore, memEnable}),
    .sysclk(clk), .Opcode(Opcode), .in_4(aluflag));
  Button Reset (.out(clr));
  Bit_Extender #(.in_width(32)) bit_extender_2 (.in(RZ), .out(bit_extender_2_out));
  Multiplexer #(.width(16), .enable("false")) multiplexer_4 (
    .in0(bit_extender_2_out), .in1(PC), .out(multiplexer_4_out), .sel(selectMUXA));
  not not_1 (not_1_out, memLoadStore);
  RAM #(.addrWidth(16), .dataWidth(32), .bus("separate")) ram_1 (
    .addr(multiplexer_4_out), .din(RMout), .data(IRin), .str(not_1_out), .sel(memEnable), .clk(clk),
    .ld(memLoadStore), .clr(Memory_Clear_out));
  Button Memory_Clear (.out(Memory_Clear_out));

  // Other names for the same wires on the sheet: memData[31:0] = IRin

  // Notes on the sheet:
  //   Five Stage Pipeline
  //   System Clock (control from here)
  //   Harsh
  //   19CS01061
  //   Instruction Address Generator
  //   Control Unit
  //   System Reset (Erase everything)
  //   Memory Interface
endmodule

// Register File
module RF (
  input  clock,
  input  clear,
  input  Enable_Writeback,
  input  [2:0] selectRA,
  input  [2:0] selectRB,
  input  [2:0] selectRC,
  input  Store,
  input  [31:0] Input_RC,
  output [31:0] Output_RA,
  output [31:0] Output_RB
);

  wire demultiplexer_1_out0, demultiplexer_1_out1, demultiplexer_1_out2, demultiplexer_1_out3,
       demultiplexer_1_out4, demultiplexer_1_out5, demultiplexer_1_out6, demultiplexer_1_out7;
  wire [2:0] multiplexer_3_out;
  wire [31:0] R0_q, R1_q, R2_q, R3_q, R4_q, R5_q, R6_q, R7_q;

  Demultiplexer #(.select(3), .enable("false")) demultiplexer_1 (
    .out0(demultiplexer_1_out0), .out1(demultiplexer_1_out1), .out2(demultiplexer_1_out2),
    .out3(demultiplexer_1_out3), .out4(demultiplexer_1_out4), .out5(demultiplexer_1_out5),
    .out6(demultiplexer_1_out6), .out7(demultiplexer_1_out7), .in(Enable_Writeback), .sel(selectRC));
  Register #(.width(32)) R0 (.D(Input_RC), .en(demultiplexer_1_out0), .Q(R0_q), .clk(clock), .clr(clear));
  Register #(.width(32)) R1 (.D(Input_RC), .en(demultiplexer_1_out1), .Q(R1_q), .clk(clock), .clr(clear));
  Register #(.width(32)) R2 (.D(Input_RC), .en(demultiplexer_1_out2), .Q(R2_q), .clk(clock), .clr(clear));
  Register #(.width(32)) R3 (.D(Input_RC), .en(demultiplexer_1_out3), .Q(R3_q), .clk(clock), .clr(clear));
  Register #(.width(32)) R4 (.D(Input_RC), .en(demultiplexer_1_out4), .Q(R4_q), .clk(clock), .clr(clear));
  Register #(.width(32)) R5 (.D(Input_RC), .en(demultiplexer_1_out5), .Q(R5_q), .clk(clock), .clr(clear));
  Register #(.width(32)) R6 (.D(Input_RC), .en(demultiplexer_1_out6), .Q(R6_q), .clk(clock), .clr(clear));
  Register #(.width(32)) R7 (.D(Input_RC), .en(demultiplexer_1_out7), .Q(R7_q), .clk(clock), .clr(clear));
  Multiplexer #(.select(3), .width(32), .enable("false")) multiplexer_1 (
    .in0(R0_q), .in1(R1_q), .in2(R2_q), .in3(R3_q), .in4(R4_q), .in5(R5_q), .in6(R6_q), .in7(R7_q),
    .out(Output_RA), .sel(selectRA));
  Multiplexer #(.select(3), .width(32), .enable("false")) multiplexer_2 (
    .in0(R0_q), .in1(R1_q), .in2(R2_q), .in3(R3_q), .in4(R4_q), .in5(R5_q), .in6(R6_q), .in7(R7_q),
    .out(Output_RB), .sel(multiplexer_3_out));
  Multiplexer #(.width(3), .enable("false")) multiplexer_3 (
    .in0(selectRB), .in1(selectRC), .out(multiplexer_3_out), .sel(Store));

  // Other names for the same wires on the sheet: clk = clock; clr = clear; enWrite = Enable_Writeback

  // Notes on the sheet:
  //   Tunnels
  //   Harsh
  //   19CS01061
  //   Register File (8 registers - 32 Bit)
endmodule

module ALU (
  input  [31:0] Input_A,
  input  [31:0] Input_B,
  input  [3:0] ALU_Control_Signal,
  output [31:0] Output_ALU,
  output out_5
);

  wire comparator_2_eq, comparator_2_gt, comparator_2_lt;
  wire [31:0] adder_1_out, and_1_out, bit_extender_1_out, bit_extender_2_out, bit_extender_3_out, or_1_out,
       subtractor_1_out;

  Comparator #(.width(32)) comparator_1 (.a(Input_A), .b({32{1'b0}}), .eq(out_5));  // open: gt, lt
  Adder #(.width(32)) adder_1 (.a(Input_A), .b(Input_B), .out(adder_1_out));  // open: cin, cout
  Subtractor #(.width(32)) subtractor_1 (.a(Input_A), .b(Input_B), .out(subtractor_1_out));  // open: bin, bout
  assign and_1_out = Input_A & Input_B;  // AND_Gate and_1, 32 bits wide
  assign or_1_out = Input_A | Input_B;  // OR_Gate or_1, 32 bits wide
  Comparator #(.width(32)) comparator_2 (
    .a(Input_A), .b(Input_B), .gt(comparator_2_gt), .eq(comparator_2_eq), .lt(comparator_2_lt));
  assign bit_extender_1_out = {{31{1'b0}}, comparator_2_gt};  // Bit_Extender bit_extender_1
  assign bit_extender_2_out = {{31{1'b0}}, comparator_2_eq};  // Bit_Extender bit_extender_2
  assign bit_extender_3_out = {{31{1'b0}}, comparator_2_lt};  // Bit_Extender bit_extender_3
  Multiplexer #(.select(4), .width(32), .enable("false")) multiplexer_1 (
    .in0(Input_A), .in1(Input_A), .in2(adder_1_out), .in3(adder_1_out), .in4(adder_1_out),
    .in5(subtractor_1_out), .in6(and_1_out), .in7(or_1_out), .in8(Input_B), .in9(bit_extender_1_out),
    .in10(bit_extender_2_out), .in11(bit_extender_3_out), .in12(Input_B), .in13(Input_B), .out(Output_ALU),
    .sel(ALU_Control_Signal));  // open: in14, in15
  // Probe on ALU_Control_Signal

  // Other names for the same wires on the sheet: ALU_select[3:0] = ALU_Control_Signal; aluflag = out_5;
  //   InA[31:0] = Input_A; InB[31:0] = Input_B; out[31:0] = Output_ALU

  // Notes on the sheet:
  //   Global Variables
  //   alu flag for Jump if Zero Instruction
  //   Harsh
  //   19CS01061
  //   Halt and Move
  //   Addition
  //   Subtraction
  //   AND operation
  //   OR operation
  //   Move Immediate
  //   Comparator
  //   Jump and Jump IF Zero
  //   Arithmetic Logical Unit
endmodule

module Control_Unit (
  input  [31:0] IR,
  input  sysclk,
  input  Clear,
  input  in_4,
  output [31:0] Immediate,
  output [4:0] Opcode,
  output [31:0] Output_Signals
);

  wire Add, And, and_2_out, and_3_out, and_5_out, and_6_out, and_7_out, eq, gt, Halt, jump, jz, lt, Move,
       MoveImm, not_1_out, not_2_out, not_3_out, Or, or_1_out, or_3_out, stage2, stage3, stage4, stage5, Sub;
  wire [2:0] Counter_q;

  Bit_Extender #(.in_width(5), .out_width(3)) bit_extender_1 (.in(IR[21:17]), .out(Output_Signals[12:10]));
  Bit_Extender #(.in_width(5), .out_width(3)) bit_extender_2 (.in(IR[16:12]), .out(Output_Signals[16:14]));
  Bit_Extender #(.in_width(5), .out_width(3)) bit_extender_3 (.in(IR[26:22]), .out(Output_Signals[20:18]));
  Decoder #(.select(3), .enable("false")) decoder_1 (
    .out0(Output_Signals[6]), .out1(stage2), .out2(stage3), .out3(stage4), .out4(stage5), .sel(Counter_q));  // open: out5, out6, out7
  Counter #(.width(3), .max('h4)) Counter (.Q(Counter_q), .clk(sysclk), .clr(Clear));  // open: load, D, count, carry
  assign Immediate = {{16{1'b0}}, IR[16:1]};  // Bit_Extender bit_extender_4
  or or_1 (or_1_out, Move, Output_Signals[4], Add, MoveImm, Sub, And, Or, gt, eq, lt);
  and and_1 (Output_Signals[7], stage5, or_1_out);
  Decoder #(.select(5), .enable("false")) decoder_2 (
    .out0(Halt), .out1(Move), .out2(Output_Signals[4]), .out3(Output_Signals[24]), .out4(Add), .out5(Sub),
    .out6(And), .out7(Or), .out8(MoveImm), .out9(gt), .out10(eq), .out11(lt), .out12(jump), .out13(jz),
    .sel(IR[31:27]));  // open: out14, out15, out16, out17, out18, out19, out20, out21, out22, out23, out24, out25, out26, out27, out28, out29, out30, out31
  and and_2 (and_2_out, stage4, jump);
  and and_3 (and_3_out, stage4, jz, in_4);
  not not_1 (not_1_out, Halt);
  not not_2 (not_2_out, and_2_out);
  and and_4 (Output_Signals[5], not_2_out, not_3_out);
  not not_3 (not_3_out, and_3_out);
  and and_5 (and_5_out, stage2, not_1_out);
  or or_2 (Output_Signals[8], and_5_out, and_2_out, and_3_out);
  or or_3 (or_3_out, Output_Signals[4], Output_Signals[24]);
  and and_6 (and_6_out, stage4, or_3_out);
  and and_7 (and_7_out, stage4, Output_Signals[4]);
  or or_4 (Output_Signals[0], Output_Signals[6], and_6_out);
  or or_5 (Output_Signals[1], Output_Signals[6], and_7_out);
  Multiplexer #(.select(5), .width(4), .enable("false")) multiplexer_1 (
    .in0(4'b0000), .in1(4'b0001), .in2(4'b0010), .in3(4'b0011), .in4(4'b0100), .in5(4'b0101), .in6(4'b0110),
    .in7(4'b0111), .in8(4'b1000), .in9(4'b1001), .in10(4'b1010), .in11(4'b1011), .in12(4'b1100),
    .in13(4'b1101), .out(Output_Signals[31:28]), .sel(IR[31:27]));  // open: in14, in15, in16, in17, in18, in19, in20, in21, in22, in23, in24, in25, in26, in27, in28, in29, in30, in31

  assign Opcode = IR[31:27];
  assign Output_Signals[3:2] = {IR[0], Output_Signals[6]};

  // Other names for the same wires on the sheet: op5 = IR[27]; op4 = IR[28]; op3 = IR[29]; op2 = IR[30]; op1 = IR[31];
  //   aluflag = in_4; clk = sysclk; clr = Clear; I11 = IR[1]; I10 = IR[2]; I9 = IR[3]; I8 = IR[4]; I7 = IR[5];
  //   I6 = IR[6]; I5 = IR[7]; I4 = IR[8]; I3 = IR[9]; I2 = IR[10]; I1 = IR[11]; B5 = IR[12]; B4 = IR[13]; B3 = IR[14];
  //   B2 = IR[15]; B1 = IR[16]; A5 = IR[17]; A4 = IR[18]; A3 = IR[19]; A2 = IR[20]; A1 = IR[21]; C5 = IR[22];
  //   C4 = IR[23]; C3 = IR[24]; C2 = IR[25]; C1 = IR[26]; memEnable = Output_Signals[0];
  //   memLoadStore = Output_Signals[1]; enImm = IR[0]; selectMUXB = IR[0]; Load = Output_Signals[4];
  //   selectMUXY = Output_Signals[4]; selectMUXPC = Output_Signals[5]; enIR = Output_Signals[6];
  //   selectMUXA = Output_Signals[6]; stage1 = Output_Signals[6]; enReWrite = Output_Signals[7];
  //   enPC = Output_Signals[8]; selectRA[2:0] = Output_Signals[12:10]; selectRB[2:0] = Output_Signals[16:14];
  //   selectRC[2:0] = Output_Signals[20:18]; Store = Output_Signals[24]; ALU_select[3:0] = Output_Signals[31:28]

  // Notes on the sheet:
  //   Tunnels
  //   Immediate Value Generation
  //   Register File Signals
  //   select bits for RF
  //   Enable Write Mode in RF
  //   Step Counter
  //   a)
  //   Instruction Register Splitting
  //   Select bit for MUXY(Load)
  //   Harsh
  //   19CS01061
  //   Decoding
  //   JZ R1(flag) R2(set)
  //   b)
  //   MUX and Enable Signals
  //   Instruction Decoding
  //   When will the PC register change ?
  //   Memory Signals
  //   When to activate memory ?
  //   When to perform Load or Store ?
  //   Output Signals
  //   ALU control signals
endmodule
